# Fritzing sketch stewart2 (saved by Fritzing 0.9.9b)
circuit board: 14.5196cm x 11.4252cm

parts:
  Part2 = LCD Display 16x2 [part_number=LCD]
  S1 = Round Pushbutton [part_number=R/S]
  S2 = Round Pushbutton [part_number=Time]
  S3 = Round Pushbutton [part_number=Pos]
  LED2 = LED - 5mm [color="Red (633nm)" current=0.030 package="5 mm [THT]"]
  LED3 = LED - 5mm [color="Red (633nm)" current=0.030 package="5 mm [THT]"]
  LED4 = LED - 5mm [color="Red (633nm)" current=0.030 package="5 mm [THT]"]
  R1 = Resistor [tolerance=±5% resistance=220 package="0805 [SMD]"]
  R3 = Resistor [tolerance=±5% resistance=220 package="0805 [SMD]"]
  R4 = Resistor [tolerance=±5% resistance=220 package="0805 [SMD]"]
  JP9 = Header 4 [package=jst-4-pth]
  JP10 = Header 4 [package=jst-4-pth]
  JP11 = Header 4 [package=jst-4-pth]
  JP12 = Header 4 [package=jst-4-pth]
  JP13 = Header 4 [package=jst-4-pth]
  JP14 = Header 4 [package=jst-4-pth]
  JP17 = Header 5 [package=jst-5-pth]
  JP18 = Header 5 [package=jst-5-pth]
  Part3 = Arduino Due (Rev2b)
  J1 = Power Jack [package=power_jack_slot]

nets:
  N1: Part2.aún_sin_nombre#0, Part2.aún_sin_nombre#4, S1.leg1, JP9.1, JP10.1, JP11.1, JP12.1, JP13.1, JP14.1
  N2: Part2.aún_sin_nombre#3, Part3.D14/TX3
  N3: Part2.aún_sin_nombre#5, Part3.D15/RX3
  N4: Part2.aún_sin_nombre#10, Part3.D16/TX2
  N5: Part2.aún_sin_nombre#11, Part3.D17/RX2
  N6: Part2.aún_sin_nombre#12, Part3.D18/TX1
  N7: Part2.aún_sin_nombre#13, Part3.D19/RX1
  N8: S1.leg0, Part3.D44
  N9: S2.leg0, Part3.D46
  GND: S2.leg1, S3.leg1, R1.Pin_0, R3.Pin_0, R4.Pin_0, Part3.GND, J1.GND
  N10: S3.leg0, Part3.D45
  N11: LED2.cathode, R4.Pin_1
  N12: LED2.anode, Part3.D3_PWM
  N13: LED3.cathode, R1.Pin_1
  N14: LED3.anode, Part3.D4_PWM/SS1
  N15: LED4.cathode, R3.Pin_1
  N16: LED4.anode, Part3.D5_PWM
  N17: JP9.2, JP10.2, JP11.2, JP12.2, JP13.2, JP14.2, J1.PWR
  N18: JP9.4, Part3.D10_PWM/SS0
  N19: JP10.4, Part3.D11_PWM
  N20: JP11.4, Part3.D6_PWM
  N21: JP12.4, Part3.D7_PWM
  N22: JP13.4, Part3.D8_PWM
  N23: JP14.4, Part3.D9_PWM
  N24: JP17.1, Part3.A2
  N25: JP17.2, Part3.A1
  N26: JP17.3, Part3.A0
  N27: JP17.4, JP18.4
  N28: JP17.5, JP18.5, Part3.IOREF
  N29: JP18.1, Part3.A5
  N30: JP18.2, Part3.A4
  N31: JP18.3, Part3.A3

custom parts:
  Header 5: Header 5 Standard 5-pin 2mm header. Rev3
